// Logisim project Main ALU.circ as structural Verilog: 5 circuits, main circuit Main
module Main (
  input  [3:0] A,
  input  [3:0] B,
  input  [2:0] CMD,
  output Over,
  output Over_2,
  output [3:0] S
);

  wire decoder_3x8_1_s0, decoder_3x8_1_s1, decoder_3x8_1_s2, decoder_3x8_1_s3, decoder_3x8_1_s4;
  wire [3:0] or_4_1_s, soma_4_1_out_4, sub_4_1_out_4;

  Decoder_3x8 decoder_3x8_1 (
    .S0(decoder_3x8_1_s0), .S1(decoder_3x8_1_s1), .S2(decoder_3x8_1_s2), .S3(decoder_3x8_1_s3),
    .S4(decoder_3x8_1_s4), .CMD(CMD));  // open: S5, S6, S7
  Buffer buffer_1 (.A(B), .A_2(decoder_3x8_1_s0), .S(S));
  Soma___4 soma_4_1 (.A(A), .out_3(Over), .B(B), .out_4(soma_4_1_out_4));
  Buffer buffer_2 (.A(soma_4_1_out_4), .A_2(decoder_3x8_1_s1), .S(S));
  Sub___4 sub_4_1 (.A(A), .Vai_1(Over_2), .in_2(B), .out_4(sub_4_1_out_4));
  Buffer buffer_3 (.A(sub_4_1_out_4), .A_2(decoder_3x8_1_s2), .S(S));
  Or_4 or_4_1 (.A(A), .B(B), .S(or_4_1_s));
  Buffer buffer_4 (.A(or_4_1_s), .A_2(decoder_3x8_1_s3), .S(S));
  Buffer_Inversor buffer_inversor_1 (.A(B), .A_2(decoder_3x8_1_s4), .S(S));
endmodule

module Buffer (
  input  [3:0] A,
  input  A_2,
  output [3:0] S
);

  assign S[1] = A_2 ? A[1] : 1'bz;  // Controlled_Buffer controlled_buffer_1
  assign S[3] = A_2 ? A[3] : 1'bz;  // Controlled_Buffer controlled_buffer_2
  assign S[2] = A_2 ? A[2] : 1'bz;  // Controlled_Buffer controlled_buffer_3
  assign S[0] = A_2 ? A[0] : 1'bz;  // Controlled_Buffer controlled_buffer_4
endmodule

module Buffer_Inversor (
  input  [3:0] A,
  input  A_2,
  output [3:0] S
);

  assign S[1] = A_2 ? ~A[1] : 1'bz;  // Controlled_Inverter controlled_inverter_1
  assign S[3] = A_2 ? ~A[3] : 1'bz;  // Controlled_Inverter controlled_inverter_2
  assign S[2] = A_2 ? ~A[2] : 1'bz;  // Controlled_Inverter controlled_inverter_3
  assign S[0] = A_2 ? ~A[0] : 1'bz;  // Controlled_Inverter controlled_inverter_4
endmodule

module Decoder_3x8 (
  input  [2:0] CMD,
  output S0,
  output S1,
  output S2,
  output S3,
  output S4,
  output S5,
  output S6,
  output S7
);

  wire not_1_out, not_2_out, not_3_out, not_4_out, not_5_out, not_6_out, not_7_out, not_8_out, not_9_out,
       not_10_out, not_11_out, not_12_out;

  not not_1 (not_1_out, CMD[2]);
  and and_1 (S0, not_1_out, not_2_out, not_3_out);
  not not_2 (not_2_out, CMD[1]);
  not not_3 (not_3_out, CMD[0]);
  not not_4 (not_4_out, CMD[2]);
  not not_5 (not_5_out, CMD[1]);
  and and_2 (S1, not_4_out, not_5_out, CMD[0]);
  not not_6 (not_6_out, CMD[2]);
  and and_3 (S2, not_6_out, CMD[1], not_7_out);
  not not_7 (not_7_out, CMD[0]);
  not not_8 (not_8_out, CMD[2]);
  and and_4 (S3, not_8_out, CMD[1], CMD[0]);
  not not_9 (not_9_out, CMD[1]);
  and and_5 (S4, CMD[2], not_9_out, not_10_out);
  not not_10 (not_10_out, CMD[0]);
  not not_11 (not_11_out, CMD[1]);
  and and_6 (S5, CMD[2], not_11_out, CMD[0]);
  and and_7 (S6, CMD[2], CMD[1], not_12_out);
  not not_12 (not_12_out, CMD[0]);
  and and_8 (S7, CMD[2], CMD[1], CMD[0]);
endmodule

module Or_4 (
  input  [3:0] A,
  input  [3:0] B,
  output [3:0] S
);

  or or_1 (S[3], A[3], B[3]);
  or or_2 (S[2], A[2], B[2]);
  or or_3 (S[1], A[1], B[1]);
  or or_4 (S[0], A[0], B[0]);
endmodule
