// Logisim project Sub - 1.circ as structural Verilog: 2 circuits, main circuit Sub - 1
module Teste_Sub___1 (
  input  B,
  input  A,
  input  in_3,
  output out_4,
  output out_5
);

  Sub___1 sub_1_1 (.A(A), .B(B), .Vem_1(in_3), .Sub(out_5), .Vai_1(out_4));
endmodule

module Sub___1 (
  input  A,
  input  B,
  input  Vem_1,
  output Sub,
  output Vai_1
);

  wire and_1_out, and_2_out, not_1_out, or_1_out, xor_1_out;

  not not_1 (not_1_out, A);
  or or_1 (or_1_out, B, Vem_1);
  xor xor_1 (xor_1_out, A, B);
  xor xor_2 (Sub, xor_1_out, Vem_1);
  and and_1 (and_1_out, or_1_out, not_1_out);
  and and_2 (and_2_out, B, Vem_1);
  or or_2 (Vai_1, and_1_out, and_2_out);
endmodule
